# Fritzing sketch ESP8266_IR (saved by Fritzing 0.9.3b)

parts:
  U1 = ESP8266 WiFi Module [part_number=ESP8266]
  R1 = Resistor [tolerance=±5% resistance=1k package=THT]
  IR1 = TSOP312.., 314.. [package=THT]
  Q1 = TRANSISTOR_NPN [package=to-92-ammo]
  R2 = Resistor [tolerance=±5% resistance=1k package=THT]
  LED1 = LED - 3mm [color="Infrared (940nm)" package="3 mm [THT]"]

nets:
  N1: U1.RXD, IR1.Data
  3.3V: U1.VCC, R1.Pin_0, IR1.Vs, LED1.anode
  N2: U1.GPIO_0, R2.Pin_0
  N3: U1.CH_PD, R1.Pin_1
  GND: U1.GND, IR1.GND, Q1.E
  N4: Q1.B, R2.Pin_1
  N5: Q1.C, LED1.cathode

custom parts:
  ESP8266 WiFi Module: Generic WiFi Module based on the ESP8266 with onboard PCB antenna and UART communications
